// Logisim project FRANK6000.circ as structural Verilog: 5 circuits, main circuit main
module main (
);

  wire and_1_out, clk_out, control_unit_1_addrin, control_unit_1_addrw, control_unit_1_aluin1,
       control_unit_1_aluin2, control_unit_1_call, control_unit_1_frin, control_unit_1_frw,
       control_unit_1_jump, control_unit_1_pcw, control_unit_1_retrn, control_unit_1_statusw,
       control_unit_1_wregw, jump_control_1_jump, reset_out;
  wire [1:0] control_unit_1_j_mode, control_unit_1_wregin, Instruction_Memory_dout_2;
  wire [2:0] alu_1_status, STATUS_q;
  wire [7:0] adder_1_out, ADDR_q, alu_1_res, File_Registers_dout, Instruction_Memory_dout,
       instruction_stack_1_stack_out, multiplexer_1_out, multiplexer_2_out, multiplexer_3_out,
       multiplexer_4_out, multiplexer_5_out, multiplexer_6_out, multiplexer_7_out, PC_q, WREG_q;
  wire [15:10] Instruction_Memory_dout_3;

  Adder adder_1 (.a(PC_q), .b(8'h1), .out(adder_1_out));  // open: cin, cout
  Clock clk (.out(clk_out));
  Button reset (.out(reset_out));
  Multiplexer #(.width(8), .enable("false")) multiplexer_1 (
    .in0(adder_1_out), .in1(Instruction_Memory_dout), .out(multiplexer_1_out), .sel(and_1_out));
  Instruction_Stack instruction_stack_1 (
    .stack_out(instruction_stack_1_stack_out), .PC_in(PC_q), .call(control_unit_1_call), .clk(clk_out),
    .rtrn(control_unit_1_retrn), .reset(reset_out));
  Register PC (.D(multiplexer_2_out), .en(control_unit_1_pcw), .clk(clk_out), .Q(PC_q), .clr(reset_out));
  Multiplexer #(.select(2), .width(8), .enable("false")) multiplexer_2 (
    .in0(adder_1_out), .in1(multiplexer_1_out), .in2(instruction_stack_1_stack_out), .out(multiplexer_2_out),
    .sel(control_unit_1_j_mode));  // open: in3
  and and_1 (and_1_out, control_unit_1_jump, jump_control_1_jump);
  RAM #(.dataWidth(16), .databus("bibus")) Instruction_Memory (
    .addr(PC_q), .we(1'b0), .oe(1'b1), .clk(clk_out),
    .dout({Instruction_Memory_dout_3, Instruction_Memory_dout_2, Instruction_Memory_dout}));  // open: din
  Jump_Control jump_control_1 (.jump(jump_control_1_jump), .opcode(Instruction_Memory_dout_2), .status(STATUS_q));
  Register ADDR (.D(multiplexer_3_out), .en(control_unit_1_addrw), .clk(clk_out), .Q(ADDR_q), .clr(reset_out));
  Multiplexer #(.width(8), .enable("false")) multiplexer_3 (
    .in0(WREG_q), .in1(alu_1_res), .out(multiplexer_3_out), .sel(control_unit_1_addrin));
  RAM #(.databus("bibus")) File_Registers (
    .addr(multiplexer_4_out), .we(control_unit_1_frw), .oe(1'b1), .clk(clk_out), .din(WREG_q),
    .dout(File_Registers_dout));
  Multiplexer #(.width(8), .enable("false")) multiplexer_4 (
    .in0(Instruction_Memory_dout), .in1(ADDR_q), .out(multiplexer_4_out), .sel(control_unit_1_frin));
  Multiplexer #(.select(2), .width(8), .enable("false")) multiplexer_5 (
    .in0(alu_1_res), .in1(Instruction_Memory_dout), .in2(File_Registers_dout), .in3(ADDR_q),
    .out(multiplexer_5_out), .sel(control_unit_1_wregin));
  Register WREG (.D(multiplexer_5_out), .en(control_unit_1_wregw), .clk(clk_out), .Q(WREG_q), .clr(reset_out));
  Multiplexer #(.width(8), .enable("false")) multiplexer_6 (
    .in0(WREG_q), .in1(ADDR_q), .out(multiplexer_6_out), .sel(control_unit_1_aluin1));
  Multiplexer #(.width(8), .enable("false")) multiplexer_7 (
    .in0(Instruction_Memory_dout), .in1(File_Registers_dout), .out(multiplexer_7_out),
    .sel(control_unit_1_aluin2));
  ALU alu_1 (
    .status(alu_1_status), .res(alu_1_res),
    .opcode({Instruction_Memory_dout_3[11:10], Instruction_Memory_dout_2}), .p(multiplexer_7_out),
    .WREG(multiplexer_6_out));
  Control_Unit control_unit_1 (
    .ADDRin(control_unit_1_addrin), .FRin(control_unit_1_frin), .STATUSw(control_unit_1_statusw),
    .ADDRw(control_unit_1_addrw), .FRw(control_unit_1_frw), .ALUin2(control_unit_1_aluin2),
    .jump(control_unit_1_jump), .ALUin1(control_unit_1_aluin1), .WREGw(control_unit_1_wregw),
    .input_control(Instruction_Memory_dout_3[15:12]), .j_mode(control_unit_1_j_mode),
    .WREGin(control_unit_1_wregin), .call(control_unit_1_call), .retrn(control_unit_1_retrn),
    .PCw(control_unit_1_pcw), .clk(clk_out), .rst(reset_out));
  Register #(.width(3)) STATUS (
    .D(alu_1_status), .en(control_unit_1_statusw), .clk(clk_out), .Q(STATUS_q), .clr(reset_out));
endmodule

module ALU (
  input  [3:0] opcode,
  input  [7:0] WREG,
  input  [7:0] p,
  output [7:0] res,
  output [2:0] status
);

  wire adder_1_cout, adder_2_cout, and_2_out, and_3_out, and_4_out, and_5_out, comparator_1_eq,
       comparator_1_lt, demultiplexer_1_out3, demultiplexer_1_out4, demultiplexer_1_out8,
       demultiplexer_1_out9, not_2_out, subtractor_1_bout, subtractor_2_bout;
  wire [7:0] adder_1_out, adder_2_out, and_1_out, bit_extender_1_out, negator_1_out, not_1_out, or_1_out,
       shifter_1_out, shifter_2_out, subtractor_1_out, subtractor_2_out, xor_1_out;

  assign not_1_out = ~WREG;  // NOT_Gate not_1, 8 bits wide
  Negator negator_1 (.in(WREG), .out(negator_1_out));
  Adder adder_1 (.a(WREG), .b(8'h1), .out(adder_1_out), .cout(adder_1_cout));  // open: cin
  Subtractor subtractor_1 (.a(WREG), .b(8'h1), .out(subtractor_1_out), .bout(subtractor_1_bout));  // open: bin
  assign and_1_out = WREG & p;  // AND_Gate and_1, 8 bits wide
  assign or_1_out = WREG | p;  // OR_Gate or_1, 8 bits wide
  assign xor_1_out = WREG ^ p;  // XOR_Gate xor_1, 8 bits wide
  Adder adder_2 (.a(WREG), .b(p), .out(adder_2_out), .cout(adder_2_cout));  // open: cin
  Subtractor subtractor_2 (.a(WREG), .b(p), .out(subtractor_2_out), .bout(subtractor_2_bout));  // open: bin
  Comparator comparator_1 (.a(WREG), .b(p), .eq(comparator_1_eq), .lt(comparator_1_lt));  // open: gt
  Shifter shifter_1 (.in(WREG), .\dist (p[2:0]), .out(shifter_1_out));
  Shifter #(.shift("lr")) shifter_2 (.in(WREG), .\dist (p[2:0]), .out(shifter_2_out));
  assign bit_extender_1_out = {{7{comparator_1_lt}}, not_2_out};  // Bit_Extender bit_extender_1
  not not_2 (not_2_out, comparator_1_eq);
  Multiplexer #(.select(4), .width(8), .enable("false")) multiplexer_1 (
    .in0({8{1'b0}}), .in1(not_1_out), .in2(negator_1_out), .in3(adder_1_out), .in4(subtractor_1_out),
    .in5(and_1_out), .in6(or_1_out), .in7(xor_1_out), .in8(adder_2_out), .in9(subtractor_2_out),
    .in10(bit_extender_1_out), .in11(shifter_1_out), .in12(shifter_2_out), .out(res), .sel(opcode));  // open: in13, in14, in15
  Demultiplexer #(.select(4), .enable("false")) demultiplexer_1 (
    .out3(demultiplexer_1_out3), .out4(demultiplexer_1_out4), .out8(demultiplexer_1_out8),
    .out9(demultiplexer_1_out9), .in(1'b1), .sel(opcode));  // open: out0, out1, out2, out5, out6, out7, out10, out11, out12, out13, out14, out15
  and and_2 (and_2_out, adder_1_cout, demultiplexer_1_out3);
  and and_3 (and_3_out, demultiplexer_1_out4, subtractor_1_bout);
  nor nor_1 (status[0], res[0], res[1], res[2], res[3], res[4], res[5], res[6], res[7]);
  and and_4 (and_4_out, adder_2_cout, demultiplexer_1_out8);
  and and_5 (and_5_out, demultiplexer_1_out9, subtractor_2_bout);
  or or_2 (status[2], and_2_out, and_3_out, and_4_out, and_5_out);

  assign status[1] = res[7];
endmodule

module Jump_Control (
  input  [1:0] opcode,
  input  [2:0] status,
  output jump
);

  wire and_1_out, and_2_out, and_3_out, decoder_1_out0, decoder_1_out1, decoder_1_out2, decoder_1_out3;

  or or_1 (jump, decoder_1_out0, and_1_out, and_2_out, and_3_out);
  and and_1 (and_1_out, decoder_1_out1, status[0]);
  and and_2 (and_2_out, decoder_1_out2, status[1]);
  and and_3 (and_3_out, decoder_1_out3, status[2]);
  Decoder #(.select(2), .enable("false")) decoder_1 (
    .out0(decoder_1_out0), .out1(decoder_1_out1), .out2(decoder_1_out2), .out3(decoder_1_out3), .sel(opcode));
endmodule

module Control_Unit (
  input  [3:0] input_control,
  input  clk,
  input  rst,
  output jump,
  output [1:0] j_mode,
  output call,
  output retrn,
  output ADDRin,
  output FRin,
  output [1:0] WREGin,
  output ALUin1,
  output ALUin2,
  output PCw,
  output ADDRw,
  output FRw,
  output WREGw,
  output STATUSw
);

  wire comparator_1_eq, comparator_2_eq, comparator_3_eq, comparator_4_eq, or_1_out;
  wire [1:0] multiplexer_1_out, multiplexer_2_out, register_1_q;
  wire [15:0] multiplexer_3_out, multiplexer_4_out;

  Comparator #(.width(4)) comparator_1 (.a(input_control), .b(4'b1100), .eq(comparator_1_eq));  // open: gt, lt
  Comparator #(.width(4)) comparator_2 (.a(input_control), .b(4'b1111), .eq(comparator_2_eq));  // open: gt, lt
  Comparator #(.width(4)) comparator_3 (.a(input_control), .b(4'b0101), .eq(comparator_3_eq));  // open: gt, lt
  Comparator #(.width(4)) comparator_4 (.a(input_control), .b(4'b0011), .eq(comparator_4_eq));  // open: gt, lt
  or or_1 (or_1_out, comparator_1_eq, comparator_2_eq, comparator_3_eq, comparator_4_eq);
  Multiplexer #(.width(2), .enable("false")) multiplexer_1 (
    .in0(2'b01), .in1(2'b00), .out(multiplexer_1_out), .sel(or_1_out));
  Register #(.width(2)) register_1 (.D(multiplexer_2_out), .en(1'b1), .clk(clk), .Q(register_1_q), .clr(rst));
  Multiplexer #(.select(2), .width(2), .enable("false")) multiplexer_2 (
    .in0(2'b01), .in1(2'b10), .in2(multiplexer_1_out), .out(multiplexer_2_out), .sel(register_1_q));  // open: in3
  Multiplexer #(.select(4), .width(16), .enable("false")) multiplexer_3 (
    .in0({16{1'b0}}), .in1(16'ha010), .in2(16'hb010), .in3(16'h800), .in4(16'h13), .in5({16{1'b0}}),
    .in6(16'h459), .in7(16'h10), .in8(16'h18), .in9(16'h214), .in10({16{1'b0}}), .in11(16'h14),
    .in12(16'h200), .in13(16'h192), .in14(16'h92), .in15({16{1'b0}}), .out(multiplexer_3_out),
    .sel(input_control));
  Multiplexer #(.select(4), .width(16), .enable("false")) multiplexer_4 (
    .in0({16{1'b0}}), .in1({16{1'b0}}), .in2({16{1'b0}}), .in3(16'h4010), .in4({16{1'b0}}), .in5(16'h33),
    .in6({16{1'b0}}), .in7({16{1'b0}}), .in8({16{1'b0}}), .in9({16{1'b0}}), .in10({16{1'b0}}),
    .in11({16{1'b0}}), .in12(16'h112), .in13({16{1'b0}}), .in14({16{1'b0}}), .in15(16'h112),
    .out(multiplexer_4_out), .sel(input_control));
  Multiplexer #(.select(2), .width(16), .enable("false")) multiplexer_5 (
    .in0({16{1'b0}}), .in1(multiplexer_3_out), .in2(multiplexer_4_out),
    .out({jump, j_mode, call, retrn, ADDRin, FRin, WREGin, ALUin1, ALUin2, PCw, ADDRw, FRw, WREGw, STATUSw}),
    .sel(register_1_q));  // open: in3
endmodule

module Instruction_Stack (
  input  rtrn,
  input  call,
  input  [7:0] PC_in,
  input  clk,
  input  reset,
  output [7:0] stack_out
);

  wire or_1_out;
  wire [3:0] adder_1_out, multiplexer_1_out, multiplexer_2_out, stack_pointer_q, subtractor_1_out;
  wire [7:0] adder_2_out;

  or or_1 (or_1_out, rtrn, call);
  Adder #(.width(4)) adder_1 (.a(stack_pointer_q), .b(4'b0001), .out(adder_1_out));  // open: cin, cout
  Register #(.width(4)) stack_pointer (
    .D(multiplexer_1_out), .en(or_1_out), .clk(clk), .Q(stack_pointer_q), .clr(reset));
  Multiplexer #(.width(4), .enable("false")) multiplexer_1 (
    .in0(subtractor_1_out), .in1(adder_1_out), .out(multiplexer_1_out), .sel(call));
  Subtractor #(.width(4)) subtractor_1 (.a(stack_pointer_q), .b(4'b0001), .out(subtractor_1_out));  // open: bin, bout
  RAM #(.addrWidth(4), .databus("bibus")) stack (
    .addr(multiplexer_2_out), .we(call), .oe(1'b1), .clk(clk), .din(adder_2_out), .dout(stack_out));
  Multiplexer #(.width(4), .enable("false")) multiplexer_2 (
    .in0(subtractor_1_out), .in1(stack_pointer_q), .out(multiplexer_2_out), .sel(call));
  Adder adder_2 (.a(8'h1), .b(PC_in), .out(adder_2_out));  // open: cin, cout
endmodule
